// Logisim project EvaluadorYRAM.circ as structural Verilog: 1 circuit, main circuit main
module main (
  input  [3:0] X,
  input  [3:0] Y,
  input  [15:0] F,
  input  Clock,
  input  Reset,
  input  write_en
);

  wire comparator_1_eq, comparator_1_gt;
  wire [15:15] MayorIgual;

  Comparator #(.width(16)) comparator_1 (
    .a(F), .b({16{1'b0}}), .gt(comparator_1_gt), .eq(comparator_1_eq));  // open: lt
  RAM #(.clearpin("true"), .dataWidth(16)) RAM_F (
    .addr({Y, X}), .we(write_en), .clk(Clock), .din(F), .clr(Reset));  // open: oe, dout
  or or_1 (MayorIgual[15], comparator_1_gt, comparator_1_eq);
  RAM #(.clearpin("true"), .dataWidth(16)) RAM_LED (
    .addr({Y, X}), .we(write_en), .clk(Clock), .din({16{MayorIgual[15]}}), .clr(Reset));  // open: oe, dout

  // Other names for the same wires on the sheet: Address[7:0] = {Y, X}; MayorIgual[14:0] = {15{MayorIgual[15]}}

  // Notes on the sheet:
  //   RAM_F
  //   RAM_LED
endmodule
