// Logisim project GeneradorPixeles.circ as structural Verilog: 1 circuit, main circuit GeneradorPixeles
module GeneradorPixeles (
  input  Reset,
  input  Clock,
  input  Start,
  output [3:0] X,
  output [3:0] Y
);

  wire contadorx_1_carry, d_ff_1_q;

  D_Flip_Flop d_ff_1 (.D(Start), .clk(Clock), .Q(d_ff_1_q), .reset(Reset));  // open: Qn, preset
  contadorX contadorx_1 (.Reset(Reset), .Enable(d_ff_1_q), .Clock(Clock), .Carry(contadorx_1_carry), .X(X));
  contadorY contadory_1 (.Reset(Reset), .Start(contadorx_1_carry), .Clock(Clock), .Y(Y));  // open: Carry
endmodule
