// Logisim project Rasterizador_grupo19.circ as structural Verilog: 1 circuit, main circuit main
module main (
  input  Start,
  input  Reset,
  input  [3:0] A,
  input  [3:0] B,
  input  [3:0] C
);

  wire Clock, LED;
  wire [3:0] not_1_out, X, Y;
  wire [15:0] decoder_1_out15, demultiplexer_1_out0, demultiplexer_1_out1, demultiplexer_1_out2,
       demultiplexer_1_out3, demultiplexer_1_out4, demultiplexer_1_out5, demultiplexer_1_out6,
       demultiplexer_1_out7, demultiplexer_1_out8, demultiplexer_1_out9, demultiplexer_1_out10,
       demultiplexer_1_out11, demultiplexer_1_out12, demultiplexer_1_out13, demultiplexer_1_out14,
       demultiplexer_1_out15, F;

  Clock clock_1 (.out(Clock));
  // Probe on X
  GeneradorPixeles generadorpixeles_1 (.Reset(Reset), .Clock(Clock), .Start(Start), .X(X), .Y(Y));
  // Probe on Y
  EvaluadorYRAM evaluadoryram_1 (
    .X(X), .Y(Y), .F(F), .Clock(Clock), .Reset(Reset), .Start(Start), .RAM_LED(LED));  // open: RAM_F
  Decoder #(.select(4)) decoder_1 (
    .out0(decoder_1_out15[15]), .out1(decoder_1_out15[14]), .out2(decoder_1_out15[13]),
    .out3(decoder_1_out15[12]), .out4(decoder_1_out15[11]), .out5(decoder_1_out15[10]),
    .out6(decoder_1_out15[9]), .out7(decoder_1_out15[8]), .out8(decoder_1_out15[7]),
    .out9(decoder_1_out15[6]), .out10(decoder_1_out15[5]), .out11(decoder_1_out15[4]),
    .out12(decoder_1_out15[3]), .out13(decoder_1_out15[2]), .out14(decoder_1_out15[1]),
    .out15(decoder_1_out15[0]), .sel(X), .en(LED));
  DotMatrix #(.inputtype("row"), .matrixcols(16), .matrixrows(16), .persist(1256)) dotmatrix_1 (
    .row0(demultiplexer_1_out0), .row1(demultiplexer_1_out1), .row2(demultiplexer_1_out2),
    .row3(demultiplexer_1_out3), .row4(demultiplexer_1_out4), .row5(demultiplexer_1_out5),
    .row6(demultiplexer_1_out6), .row7(demultiplexer_1_out7), .row8(demultiplexer_1_out8),
    .row9(demultiplexer_1_out9), .row10(demultiplexer_1_out10), .row11(demultiplexer_1_out11),
    .row12(demultiplexer_1_out12), .row13(demultiplexer_1_out13), .row14(demultiplexer_1_out14),
    .row15(demultiplexer_1_out15));
  Demultiplexer #(.select(4), .width(16)) demultiplexer_1 (
    .out0(demultiplexer_1_out0), .out1(demultiplexer_1_out1), .out2(demultiplexer_1_out2),
    .out3(demultiplexer_1_out3), .out4(demultiplexer_1_out4), .out5(demultiplexer_1_out5),
    .out6(demultiplexer_1_out6), .out7(demultiplexer_1_out7), .out8(demultiplexer_1_out8),
    .out9(demultiplexer_1_out9), .out10(demultiplexer_1_out10), .out11(demultiplexer_1_out11),
    .out12(demultiplexer_1_out12), .out13(demultiplexer_1_out13), .out14(demultiplexer_1_out14),
    .out15(demultiplexer_1_out15), .in(decoder_1_out15), .sel(not_1_out));
  assign not_1_out = ~Y;  // NOT_Gate not_1, 4 bits wide
  // Probe on F
  CalculoF calculof_1 (.Clock(Clock), .Reset(Reset), .Start(Start), .Y(Y), .X(X), .A(A), .B(B), .C(C), .ValorF(F));
endmodule
