// Logisim project contadorX.circ as structural Verilog: 1 circuit, main circuit contadorX
module contadorX (
  input  Clock,
  output Reset,
  output [3:0] X
);

  Counter #(.max('hf), .width(4)) counter_1 (.clk(Clock), .carry(Reset), .Q(X));  // open: clr, load, up, count, D
endmodule
