// Logisim project contadorY.circ as structural Verilog: 1 circuit, main circuit contadorY
module contadorY (
  input  Clock,
  output [3:0] Y
);

  Counter #(.max('hf), .trigger("falling"), .width(4)) counter_1 (
    .clk(Clock), .Q(Y));  // open: clr, load, up, count, D, carry
endmodule
